# Fritzing sketch sketch (saved by Fritzing 0.9.3b)
breadboards: 1

parts:
  Part1 = Breakout Board for Electret Microphone
  Part2 = Arduino Mega 2560 (Rev3)
  KEYPAD1 = Membrane Matrix Keypad
  U1 = LCD-16X2 [package=lcd-16x2]
  R1 = Resistor [tolerance=±5% resistance=220 package=THT]
  R2 = Trimmer Potentiometer [maximum_resistance=10kΩ package=THT]
  SPKR1 = Loudspeaker

nets:
  N1: Part1.VCC, Part2.A0
  GND: Part1.GND, Part2.GND, U1.VSS, U1.R_W, U1.K, R2.leg1, SPKR1.pin1
  5V: Part1.AUD, Part2.5V, U1.VDD, R2.leg2
  N2: Part2.D12_PWM, U1.RS
  N3: Part2.D11_PWM, U1.E
  N4: Part2.D10_PWM, SPKR1.pin2
  N5: Part2.D2_PWM, U1.DB7
  N6: Part2.D3_PWM, U1.DB6
  N7: Part2.D4_PWM, U1.DB5
  N8: Part2.D5_PWM, U1.DB4
  N9: Part2.D22, KEYPAD1.1
  N10: Part2.D24, KEYPAD1.2
  N11: Part2.D26, KEYPAD1.3
  N12: Part2.D28, KEYPAD1.4
  N13: Part2.D30, KEYPAD1.5
  N14: Part2.D32, KEYPAD1.6
  N15: Part2.D34, KEYPAD1.7
  N16: U1.VO, R2.wiper
  N17: U1.A, R1.Pin_1

custom parts:
  Membrane Matrix Keypad: Membrane Matrix 3x4 Keypad
